# Fritzing sketch FUll sketch (saved by Fritzing 0.9.3b)
breadboards: 1

parts:
  Part1 = Arduino Uno (Rev3)  # not connected
  Part2 = Arduino USB Host Shield
  IC1 = L293D [package=THT]
  VCC1 = Battery block 9V  # not connected
  VCC2 = Battery block 9V  # not connected
  VCC3 = Battery block 9V  # not connected
  VCC4 = Battery block 9V  # not connected
  VCC5 = Battery block 9V
  M1 = DC Motor
  M2 = DC Motor
  J1 = Basic Servo

nets:
  N1: Part2.5V-ARDUINO, IC1.+V, J1.vcc
  N2: Part2.D2, IC1.In_4
  N3: Part2.D3, IC1.In_3
  N4: Part2.D4, IC1.In_2
  N5: Part2.D5, IC1.In_1
  N6: Part2.D6, IC1.Enable_1
  GND: Part2.GND, IC1.0V, VCC5.-, J1.gnd
  N7: Part2.RX, J1.pulse
  N8: Part2.TX, IC1.Enable_2
  N9: IC1.Out_1_(_Controlled_by_Enable_1_), M2.pin_2
  N10: IC1.Out_2_(_Controlled_by_Enable_1_), M2.pin_1
  N11: IC1.+Vmotor, VCC5.+
  N12: IC1.Out_3_(_Controlled_by_Enable_2_), M1.pin_2
  N13: IC1.Out_4_(_Controlled_by_Enable_2_), M1.pin_1

notes:
  White wire: Input wires for Motors
  Orange wire: Enable pin(On/Off Switch)
  Black wire: GND
  Red wire: 5V
